# Fritzing sketch led_strip_circuit_diagram (saved by Fritzing 0.9.3b)
circuit board: 8.46667cm x 5.64444cm
breadboards: 1

parts:
  Arduino_1 = Arduino Nano (Rev3.0) (ICSP)
  Threshold_Microphone = Adafruit_Microphone
  Analog_Microphone = Adafruit_Microphone
  Arduino_2 = Arduino Nano (Rev3.0) (ICSP)
  Bluetooth_Module = Bluetooth HC-05 Macho
  Q1 = DC Power [voltage=5]
  LED0 = ws2812b [package="smd 2812b"]
  LED1 = ws2812b [package="smd 2812b"]
  LED300 = ws2812b [package="smd 2812b"]

nets:
  GND: Arduino_1.GND, Threshold_Microphone.connector9, Analog_Microphone.connector9, Arduino_2.GND, Bluetooth_Module.GND, Q1.V-, LED0.VSS, LED1.VSS, LED300.VSS
  N1: Arduino_1.D3, Arduino_2.D6
  N2: Arduino_1.D6, LED0.DIN
  5V: Arduino_1.VIN, Threshold_Microphone.connector8, Analog_Microphone.connector8, Arduino_2.VIN, Bluetooth_Module.VCC, Q1.V+, LED0.VDD, LED1.VDD, LED300.VDD
  N3: Arduino_1.A5, Arduino_2.A5
  N4: Arduino_1.A4, Arduino_2.A4
  N5: Threshold_Microphone.connector10, Arduino_2.D3
  N6: Analog_Microphone.connector10, Arduino_2.A7
  N7: Arduino_2.D4, Bluetooth_Module.RXD
  N8: Arduino_2.D5, Bluetooth_Module.TXD
  N9: LED0.DOUT, LED1.DIN
  N10: LED1.DOUT, LED300.DIN

notes:
  ...
  _
